// Logisim project control-logic.circ as structural Verilog: 1 circuit, main circuit control_logic
module control_logic (
  input  [31:0] Instruction,
  input  BrEq,
  input  BrLt,
  output PCSel,
  output RegWEn,
  output [2:0] ImmSel,
  output BrUn,
  output ASel,
  output BSel,
  output [3:0] ALUSel,
  output MemRW,
  output [1:0] WBSel
);

  wire and_1_out, and_2_out, and_3_out, and_4_out, and_5_out, and_6_out, and_7_out, and_8_out, and_13_out,
       and_16_out, and_17_out, and_29_out, and_30_out, and_31_out, and_32_out, and_33_out, and_34_out,
       funct3_000, funct3_001, funct3_010, funct3_011, funct3_100, funct3_101, funct3_110, funct3_111,
       funct7_0000000, funct7_0000001, funct7_0100000, is_add, is_addi, is_and, is_andi, is_auipc, is_beq,
       is_bge, is_bgeu, is_blt, is_bltu, is_bne, is_jal, is_jalr, is_lb, is_lh, is_lui, is_lw, is_mul,
       is_mulh, is_mulhu, is_or, is_ori, is_sb, is_sh, is_sll, is_slli, is_slt, is_slti, is_sub, is_sw,
       is_xor, is_xori, is_xra, is_xrai, is_xrl, is_xrli, opcode_0000011, opcode_0010011, opcode_0100011,
       opcode_0110011, opcode_1100011;
  wire [5:0] ROMInput;
  wire [15:14] rom_1_data;

  Decoder #(.select(3)) decoder_1 (
    .out0(funct3_000), .out1(funct3_001), .out2(funct3_010), .out3(funct3_011), .out4(funct3_100),
    .out5(funct3_101), .out6(funct3_110), .out7(funct3_111), .sel(Instruction[14:12]));  // open: en
  Comparator #(.mode("unsigned"), .width(7)) comparator_1 (
    .a(Instruction[6:0]), .b(7'b0110011), .eq(opcode_0110011));  // open: gt, lt
  Comparator #(.mode("unsigned"), .width(7)) comparator_2 (
    .a(Instruction[6:0]), .b(7'b0000011), .eq(opcode_0000011));  // open: gt, lt
  Comparator #(.mode("unsigned"), .width(7)) comparator_3 (
    .a(Instruction[6:0]), .b(7'b0010011), .eq(opcode_0010011));  // open: gt, lt
  Comparator #(.mode("unsigned"), .width(7)) comparator_4 (
    .a(Instruction[6:0]), .b(7'b0100011), .eq(opcode_0100011));  // open: gt, lt
  Comparator #(.mode("unsigned"), .width(7)) comparator_5 (
    .a(Instruction[6:0]), .b(7'b1100011), .eq(opcode_1100011));  // open: gt, lt
  Comparator #(.mode("unsigned"), .width(7)) comparator_6 (
    .a(Instruction[6:0]), .b(7'b0010111), .eq(is_auipc));  // open: gt, lt
  Comparator #(.mode("unsigned"), .width(7)) comparator_7 (
    .a(Instruction[6:0]), .b(7'b0110111), .eq(is_lui));  // open: gt, lt
  Comparator #(.mode("unsigned"), .width(7)) comparator_8 (
    .a(Instruction[6:0]), .b(7'b1101111), .eq(is_jal));  // open: gt, lt
  Comparator #(.mode("unsigned"), .width(7)) comparator_9 (
    .a(Instruction[6:0]), .b(7'b1100111), .eq(is_jalr));  // open: gt, lt
  Comparator #(.mode("unsigned"), .width(7)) comparator_10 (
    .a(Instruction[31:25]), .b({7{1'b0}}), .eq(funct7_0000000));  // open: gt, lt
  Comparator #(.mode("unsigned"), .width(7)) comparator_11 (
    .a(Instruction[31:25]), .b(7'b0000001), .eq(funct7_0000001));  // open: gt, lt
  Comparator #(.mode("unsigned"), .width(7)) comparator_12 (
    .a(Instruction[31:25]), .b(7'b0100000), .eq(funct7_0100000));  // open: gt, lt
  ROM #(.addrWidth(6), .dataWidth(16)) rom_1 (
    .addr(ROMInput), .data({rom_1_data, WBSel, MemRW, ALUSel, BSel, ASel, BrUn, ImmSel, RegWEn}));
  and and_1 (and_1_out, opcode_0110011, funct3_000);
  and and_2 (and_2_out, opcode_0110011, funct3_001);
  and and_3 (and_3_out, opcode_0110011, funct3_011);
  and and_4 (and_4_out, opcode_0110011, funct3_010);
  and and_5 (and_5_out, opcode_0110011, funct3_100);
  and and_6 (and_6_out, opcode_0110011, funct3_101);
  and and_7 (and_7_out, opcode_0110011, funct3_110);
  and and_8 (and_8_out, opcode_0110011, funct3_111);
  and and_9 (is_lb, opcode_0000011, funct3_000);
  and and_10 (is_lh, opcode_0000011, funct3_001);
  and and_11 (is_lw, opcode_0000011, funct3_010);
  and and_12 (is_addi, opcode_0010011, funct3_000);
  and and_13 (and_13_out, opcode_0010011, funct3_001);
  and and_14 (is_slti, opcode_0010011, funct3_010);
  and and_15 (is_xori, opcode_0010011, funct3_100);
  and and_16 (and_16_out, opcode_0010011, funct3_101);
  and and_17 (and_17_out, opcode_0010011, funct3_101);
  and and_18 (is_ori, opcode_0010011, funct3_110);
  and and_19 (is_andi, opcode_0010011, funct3_111);
  and and_20 (is_sb, opcode_0100011, funct3_000);
  and and_21 (is_sh, opcode_0100011, funct3_001);
  and and_22 (is_sw, opcode_0100011, funct3_010);
  and and_23 (is_beq, opcode_1100011, funct3_000);
  and and_24 (is_bne, opcode_1100011, funct3_001);
  and and_25 (is_blt, opcode_1100011, funct3_100);
  and and_26 (is_bge, opcode_1100011, funct3_101);
  and and_27 (is_bltu, opcode_1100011, funct3_110);
  and and_28 (is_bgeu, opcode_1100011, funct3_111);
  and and_29 (and_29_out, is_beq, BrEq);
  and and_30 (and_30_out, is_bne, ~BrEq);  // AND_Gate
  and and_31 (and_31_out, is_blt, BrLt);
  and and_32 (and_32_out, is_bge, ~BrLt);  // AND_Gate
  and and_33 (and_33_out, is_bltu, BrLt);
  and and_34 (and_34_out, is_bgeu, ~BrLt);  // AND_Gate
  and and_35 (is_add, and_1_out, funct7_0000000);
  and and_36 (is_mul, and_1_out, funct7_0000001);
  and and_37 (is_sub, and_1_out, funct7_0100000);
  and and_38 (is_sll, and_2_out, funct7_0000000);
  and and_39 (is_mulh, and_2_out, funct7_0000001);
  and and_40 (is_mulhu, and_3_out, funct7_0000001);
  and and_41 (is_slt, and_4_out, funct7_0000000);
  and and_42 (is_xor, and_5_out, funct7_0000000);
  and and_43 (is_xrl, and_6_out, funct7_0000000);
  and and_44 (is_xra, and_6_out, funct7_0100000);
  and and_45 (is_or, and_7_out, funct7_0000000);
  and and_46 (is_and, and_8_out, funct7_0000000);
  and and_47 (is_slli, and_13_out, funct7_0000000);
  and and_48 (is_xrli, and_16_out, funct7_0000000);
  and and_49 (is_xrai, and_17_out, funct7_0100000);
  or or_1 (PCSel, and_29_out, and_30_out, and_31_out, and_32_out, and_33_out, and_34_out, is_jal, is_jalr);
  Priority_Encoder #(.select_enc(6)) priority_encoder_1 (
    .in0(is_add), .in1(is_mul), .in2(is_sub), .in3(is_sll), .in4(is_mulh), .in5(is_mulhu), .in6(is_slt),
    .in7(is_xor), .in8(is_xrl), .in9(is_xra), .in10(is_or), .in11(is_and), .in12(is_lb), .in13(is_lh),
    .in14(is_lw), .in15(is_addi), .in16(is_slli), .in17(is_slti), .in18(is_xori), .in19(is_xrli),
    .in20(is_xrai), .in21(is_ori), .in22(is_andi), .in23(is_sb), .in24(is_sh), .in25(is_sw), .in26(is_beq),
    .in27(is_bne), .in28(is_blt), .in29(is_bge), .in30(is_bltu), .in31(is_bgeu), .in32(is_auipc),
    .in33(is_lui), .in34(is_jal), .in35(is_jalr), .out(ROMInput));  // open: in36, in37, in38, in39, in40, in41, in42, in43, in44, in45, in46, in47, in48, in49, in50, in51, in52, in53, in54, in55, in56, in57, in58, in59, in60, in61, in62, in63, gs, en_out, en_in

  // Other names for the same wires on the sheet: opcode[6:0] = Instruction[6:0]; funct3[2:0] = Instruction[14:12];
  //   funct7[6:0] = Instruction[31:25]; opcode_0010111 = is_auipc; opcode_0110111 = is_lui; opcode_1100111 = is_jalr;
  //   opcode_1101111 = is_jal

  // Notes on the sheet:
  //   INPUTS to your circuit
  //   Connect ROM Input here ->
  //   contents of rom_1 (hex, n*v repeats v):
  //   1001 1401 1601 1081 1481 1581 1101 1201 1281 1681 1301 1381 41 41 41 1041 10c1 1141 1241 12c1 16c1
  //   1341 13c1 842 842 842 4*64 74 74 1067 17c7 2069 2041
  //   ROM FOR CONTROL LOGIC
  //   DON'T CHANGE THE LOCATIONS OF THE INPUTS AND OUTPUTS!
  //   This is only if you choose to do the ROM option
  //   CONNECT
  //   WIRE
  //   TO
  //   USE
  //   ROM
  //   OUTPUT from your circuit
  //   Reminder: If using ROM, use combinational logic for PCSel
endmodule
