// Logisim project partial-store.circ as structural Verilog: 1 circuit, main circuit partial_store
module partial_store (
  input  [31:0] Instruction,
  input  [31:0] MemAddress,
  input  [31:0] DataFromReg,
  input  MemRW,
  output [3:0] MemWriteMask,
  output [31:0] DataToMem
);

  wire [3:0] multiplexer_3_out, multiplexer_4_out, multiplexer_6_out;
  wire [7:0] undriven, undriven_2, undriven_3;
  wire [31:0] multiplexer_1_out, multiplexer_2_out;

  Multiplexer #(.select(2), .width(32)) multiplexer_1 (
    .in0({{24{1'b0}}, DataFromReg[7:0]}), .in1({undriven_3, undriven_2, DataFromReg[7:0], undriven}),
    .in2({{8{1'b0}}, DataFromReg[7:0], {16{1'b0}}}), .in3({DataFromReg[7:0], {24{1'b0}}}),
    .out(multiplexer_1_out), .sel(MemAddress[1:0]));
  Multiplexer #(.select(2), .width(32)) multiplexer_2 (
    .in0({{16{1'b0}}, DataFromReg[15:0]}), .in1({{8{1'b0}}, DataFromReg[15:0], {8{1'b0}}}),
    .in2({DataFromReg[15:0], {16{1'b0}}}), .out(multiplexer_2_out), .sel(MemAddress[1:0]));  // open: in3
  Multiplexer #(.select(2), .width(4)) multiplexer_3 (
    .in0(4'b0001), .in1(4'b0010), .in2(4'b0100), .in3(4'b1000), .out(multiplexer_3_out), .sel(MemAddress[1:0]));
  Multiplexer #(.select(2), .width(4)) multiplexer_4 (
    .in0(4'b0011), .in1(4'b0110), .in2(4'b1100), .out(multiplexer_4_out), .sel(MemAddress[1:0]));  // open: in3
  Multiplexer #(.select(3), .width(32)) multiplexer_5 (
    .in0(multiplexer_1_out), .in1(multiplexer_2_out), .in2(DataFromReg), .out(DataToMem),
    .sel(Instruction[14:12]));  // open: in3, in4, in5, in6, in7
  Multiplexer #(.select(3), .width(4)) multiplexer_6 (
    .in0(multiplexer_3_out), .in1(multiplexer_4_out), .in2(4'b1111), .out(multiplexer_6_out),
    .sel(Instruction[14:12]));  // open: in3, in4, in5, in6, in7
  assign MemWriteMask = multiplexer_6_out & {4{MemRW}};  // AND_Gate and_1, 4 bits wide

  // Notes on the sheet:
  //   INPUTS to your circuit
  //   DON'T CHANGE THE LOCATIONS OF THE INPUTS AND OUTPUTS!
  //   OUTPUT from your circuit
endmodule
